# Fritzing sketch BPL_32_v0.1 (saved by Fritzing 0.9.3b)
circuit board: 8.46667cm x 5.64444cm

parts:
  J1 = female pin header, 18 pins [form="♀ (female)"]  # not connected
  J2 = female pin header, 18 pins [form="♀ (female)"]  # not connected
  J3 = female pin header, 5 pins [form="♀ (female)" part_number=ROT1]
  PWR = Screw terminal - 2 pins [package=THT]
  PMP/LED = Screw terminal - 2 pins [package=THT]
  PMP/ACT = Screw terminal - 2 pins [package=THT]
  D1 = Rectifier Diode [part_number=1N5400 breakdown_voltage=3.6V package="300 mil [THT]"]
  C1 = Electrolytic Capacitor [capacitance=0.22mF package="100 mil [THT, electrolytic]"]
  Q1 = Basic FET P-Channel [part_number=78S05 package="TO220 [THT]"]
  C2 = Electrolytic Capacitor [capacitance=1µF package="100 mil [THT, electrolytic]"]
  R1 = Resistor [tolerance=±5% resistance=560 package=THT]

nets:
  N1: J3.pin1, PWR.pin1, PMP/LED.pin1, PMP/ACT.pin1, C1.-, Q1.gate, C2.-
  N2: PWR.pin2, D1.anode, R1.Pin_0
  N3: PMP/LED.pin2, R1.Pin_1
  N4: D1.cathode, C1.+, Q1.source
  N5: Q1.drain, C2.+

notes:
  3.3
  CLK
  SD0
  SD1
  D0
  D1S
  D2
  D4
  RX0
  TX2
  D5
  D18
  D21
  D19
  RX2
  D12
  D32
  D25
  D34
  D33
  D35
  GND
  D13
  D14
  CMD
  SD2
  D26
  SD3
  D27
  VIN
  TX0
  D22
  D23
  EN
  VN
  VP
  +
  DATA
  SW
